# Fritzing sketch UltraSchallSensorWiring (saved by Fritzing 0.9.3b)
breadboards: 1

parts:
  Part1 = Arduino Nano (Rev3.0)
  U1 = LCD-16X2 [package=lcd-16x2_noholes]
  hc-sr1 = hc-sr04
  LCM1602_IIC1 = LCM1602 IIC [part_number="LCM1602 IIC" chip_label="LCM1602 IIC" package="DIP (Dual Inline) [THT]"]

nets:
  GND: Part1.GND, hc-sr1.GND
  N1: Part1.D7, hc-sr1.Trig
  N2: Part1.D8, hc-sr1.Echo
  5V: Part1.5V, LCM1602_IIC1.VCC
  N3: Part1.A5, LCM1602_IIC1.SCL
  N4: Part1.A4, LCM1602_IIC1.SDA
  VSS: U1.VSS, LCM1602_IIC1.VSS
  N5: U1.RS, LCM1602_IIC1.RS
  N6: U1.R_W, LCM1602_IIC1.RW
  N7: U1.E, LCM1602_IIC1.E
  N8: U1.DB0, LCM1602_IIC1.D0
  N9: U1.DB1, LCM1602_IIC1.D1
  N10: U1.DB2, LCM1602_IIC1.D2
  N11: U1.DB3, LCM1602_IIC1.D3
  N12: U1.DB4, LCM1602_IIC1.D4
  N13: U1.DB5, LCM1602_IIC1.D5
  N14: U1.DB6, LCM1602_IIC1.D6
  N15: U1.DB7, LCM1602_IIC1.D7
  N16: U1.A, LCM1602_IIC1.A
  N17: U1.K, LCM1602_IIC1.K

custom parts:
  LCM1602 IIC: I2C-Module to use a 1602 or 2004 LCD on with the wire.h libory Serial LCD Modul
